# Fritzing sketch IrrigationCircuit (saved by Fritzing 1.0.7)
stripboards: 2

parts:
  T1 = Pushbutton [package=THT]
  T2 = Pushbutton [package=THT]
  T3 = Pushbutton [package=THT]
  T4 = Pushbutton [package=THT]
  T5 = Pushbutton [package=THT]
  T6 = Pushbutton [package=THT]
  T7 = Pushbutton [package=THT]
  T8 = Pushbutton [package=THT]
  T9 = Pushbutton [package=THT]
  T10 = Pushbutton [package=THT]
  A1 = ESP32 DevKitc V4
  R4 = Resistor [tolerance=±5% power=0.25W resistance=10k package=THT]
  R6 = Resistor [tolerance=±5% power=0.25W resistance=10k package=THT]
  R7 = Resistor [tolerance=±5% power=0.25W resistance=10k package=THT]
  R8 = Resistor [tolerance=±5% power=0.25W resistance=10k package=THT]

nets:
  N1: T1.leg0, A1.Pin_26
  N2: T1.leg1, T2.leg1, T3.leg1, T4.leg1, T5.leg1, T6.leg1, T7.leg1, T8.leg1, T9.leg1, T10.leg1, A1.Pin_1
  N3: T2.leg0, A1.Pin_15
  N4: T3.leg0, A1.Pin_12
  N5: T4.leg0, A1.Pin_11
  N6: T5.leg0, A1.Pin_7
  N7: T6.leg0, A1.Pin_8
  N8: T7.leg0, R6.Pin_1
  N9: T8.leg0, R4.Pin_1
  N10: T9.leg0, A1.Pin_3, R8.Pin_1
  N11: T10.leg0, A1.Pin_4, R7.Pin_1
  N12: A1.Pin_38, R4.Pin_0, R6.Pin_0, R7.Pin_0, R8.Pin_0

custom parts:
  ESP32 DevKitc V4: ESP32-DevKitC board with ESP32-WROOM-32 module. ESP32-DevKitC V4 is a small-sized ESP32-based development board produced by Espressif. Most of the pins on the ESP module are broken out to the pin headers on the board. The pins D0, D1, D2, D3, CMD and CLK are used internally for communication between ESP32 and SPI flash memory. They are grouped on both sides near the USB connector. Avoid using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
